# Fritzing sketch Power Servo PCB (saved by Fritzing 0.9.9b)
circuit board: 4cm x 4cm
breadboards: 1

parts:
  SERVO = Header 3 [package=screwterminal-3.5mm-3_lock.007s]
  LED1 = LED - 5mm [color="Red (633nm)" current=0.030 package="5 mm [THT]"]
  R1 = Resistor [tolerance=±5% resistance=330 package=THT]
  SIGNAL_IN = Header 3 [package=screwterminal-3.5mm-3_lock.007s]
  C2 = Capacitor Polarized [package=cpol-radial-1000uf-25v]
  J2 = Power Jack [package=power_jack_pth]

nets:
  N1: SERVO.1, LED1.cathode, SIGNAL_IN.2, C2.-, J2.GND
  N2: SERVO.2, R1.Pin_1, SIGNAL_IN.1, C2.+, J2.PWR
  N3: SERVO.3, SIGNAL_IN.3
  N4: LED1.anode, R1.Pin_0
